# Fritzing sketch ir_copy (saved by Fritzing 0.9.3b)
circuit board: 8.46667cm x 5.64444cm
breadboards: 1

parts:
  U3 = ESP8266 WiFi Module [part_number=ESP8266]
  RST = Toggle Switch [package=THT]
  IR_Receiver = TSOP312.., 314.. [package=THT]
  IR_Emitter = LEDs [package=led10mm]
  S1 = Toggle Switch [package=THT]
  Composant1 = FTDI Basic Programmer

nets:
  N1: U3.RXD, Composant1.TXO
  3.3V: U3.VCC, U3.CH_PD, RST.L1, IR_Receiver.Vs, IR_Emitter.A, Composant1.POWER
  N2: U3.GPIO_0, S1.COM
  N3: U3.RST, RST.COM
  N4: U3.GPIO_2, IR_Receiver.Data
  GND: U3.GND, RST.L2, IR_Receiver.GND, S1.L2, Composant1.GND
  N5: U3.TXD, Composant1.RXI
  N6: IR_Emitter.C, S1.L1

notes:
  Normal : RST a 3.3
  RST -> GND pour reset
  GPIO-0 -> GND : Upload mode
  Reset (VCC : Normal, GND : Reset)
  Upload (GND : Upload mode)

custom parts:
  ESP8266 WiFi Module: Generic WiFi Module based on the ESP8266 with onboard PCB antenna and UART communications
